# Fritzing sketch schema (saved by Fritzing 0.6.5b)
breadboards: 1

parts:
  U1 = Optocoupler [package=THT]
  U2 = Optocoupler [package=THT]
  Arduino1 = Arduino
  R1 = Resistor [tolerance=±5% resistance=220 package="0603 [SMD]"]
  R2 = Resistor [tolerance=±5% resistance=220 package="0603 [SMD]"]
  J1 = Basic Servo
  Appareil_photo = screw terminal, 3 pins
  Ultra-son = screw terminal, 3 pins
  Led_focus = yellow LED - 5mm
  DI1 = 7-Segment LED Display [package=THT]  # not connected
  DI3 = 7-Segment LED Display [package=THT]  # not connected
  DI4 = 7-Segment LED Display [package=THT]  # not connected
  DI5 = 7_Segment_LED_Display
  Led_Shoot1 = Red LED - 5mm

nets:
  N1: U1.Pin_1, R2.Pin_1
  GND: U1.Pin_2, U2.Pin_2, Arduino1.GND, J1.gnd, Ultra-son.pin1, DI5.connector2
  N2: U1.Pin_4, U2.Pin_4, Appareil_photo.pin3
  N3: U1.Pin_5, Appareil_photo.pin1
  N4: U2.Pin_1, R1.Pin_1
  N5: U2.Pin_5, Appareil_photo.pin2
  N6: Arduino1.D10, J1.pulse
  N7: Arduino1.D9, Ultra-son.pin2
  N8: Arduino1.D6, Led_Shoot1.anode
  N9: Arduino1.D5, Led_focus.anode
  N10: Arduino1.D3, DI5.connector4
  5V: Arduino1.+5V, J1.vcc, Ultra-son.pin3, DI5.connector3, DI5.connector5
  N11: R1.Pin_0, Led_focus.cathode
  N12: R2.Pin_0, Led_Shoot1.cathode

notes:
  Appareil Photo
  Rouge [Shoot]
  Jaune [Focus]
  Blanc [Ground]
  Ultra Son
  Rouge [+]
  Violet [data]
  Noir [-]
